// Logisim project regfile.circ as structural Verilog: 1 circuit, main circuit RegFile
module RegFile (
  input  [4:0] RD,
  input  [4:0] RS1,
  input  [4:0] RS1_2,
  input  [4:0] RS2,
  input  [31:0] W,
  input  WE,
  input  Clk,
  output [31:0] s0,
  output [31:0] s1,
  output [31:0] t0,
  output [31:0] t1,
  output [31:0] a0,
  output [31:0] ra,
  output [31:0] sp,
  output [31:0] R1,
  output [31:0] R2
);

  wire decoder_1_out1, decoder_1_out3, decoder_1_out5, decoder_1_out7, decoder_1_out9, decoder_1_out11,
       decoder_1_out17, undriven, undriven_2, undriven_3, undriven_4, undriven_5, undriven_6, undriven_7,
       undriven_8;

  Decoder #(.select(5)) decoder_1 (
    .out1(decoder_1_out1), .out3(decoder_1_out3), .out5(decoder_1_out5), .out7(decoder_1_out7),
    .out9(decoder_1_out9), .out11(decoder_1_out11), .out17(decoder_1_out17), .en(RD[0]));  // open: out0, out2, out4, out6, out8, out10, out12, out13, out14, out15, out16, out18, out19, out20, out21, out22, out23, out24, out25, out26, out27, out28, out29, out30, out31, sel
  // AND_Gate and_1 has open pins: in0=WE, in4=decoder_1_out1, out=open
  // AND_Gate and_2 has open pins: in0=WE, in4=decoder_1_out17, out=open
  // AND_Gate and_3 has open pins: in0=WE, in4=decoder_1_out3, out=open
  // AND_Gate and_4 has open pins: in0=WE, in4=decoder_1_out5, out=open
  // AND_Gate and_5 has open pins: in0=WE, in4=decoder_1_out7, out=open
  // AND_Gate and_6 has open pins: in0=WE, in4=decoder_1_out9, out=open
  // AND_Gate and_7 has open pins: in0=WE, in4=decoder_1_out11, out=open
  Register #(.width(32)) Zero (.clk(undriven));  // open: D, en, Q, clr
  Register #(.width(32)) u_ra (.clk(undriven_2));  // open: D, en, Q, clr
  Register #(.width(32)) u_sp (.clk(undriven_3));  // open: D, en, Q, clr
  Register #(.width(32)) u_t0 (.clk(undriven_4));  // open: D, en, Q, clr
  Register #(.width(32)) u_t1 (.clk(undriven_5));  // open: D, en, Q, clr
  Register #(.width(32)) u_s0 (.clk(undriven_6));  // open: D, en, Q, clr
  Register #(.width(32)) u_s1 (.clk(undriven_7));  // open: D, en, Q, clr
  Register #(.width(32)) u_a0 (.clk(undriven_8));  // open: D, en, Q, clr
  Register #(.width(32)) a1 (.clk(W[0]));  // open: D, en, Q, clr
  // Pins of 1 and 5 bits meet at RD
  // Pins of 1 and 32 bits meet at W

  // Other names for the same wires on the sheet: RS1_t[4:0] = RS1_2

  // Notes on the sheet:
  //   Write Register
  //   Read Register 1
  //   Read Register 2
  //   Write Data
  //   Write Enable
  //   Clock
  //   NOTE
  //   Please do not modify/replace/move/change/delete/etc input and output pins
  //   These are debug/test outputs from your circuit
  //   Read Data 1
  //   Read Data 2
endmodule
